// Logisim project exp6-1c.circ as structural Verilog: 1 circuit, main circuit main
module main (
  input  [2:0] ABC,
  output out_2
);

  Multiplexer #(.select(3), .width(1)) multiplexer_1 (
    .in1(1'b1), .in3(1'b1), .in5(1'b1), .in6(1'b1), .out(out_2), .sel(ABC));  // open: in0, in2, in4, in7
endmodule
