// Logisim project exp6-2c.circ as structural Verilog: 1 circuit, main circuit main
module main (
  input  Data,
  input  CLK,
  input  CLR
);

  wire bcd_to_7_segment_decoder_1_p5, bcd_to_7_segment_decoder_1_p6, bcd_to_7_segment_decoder_1_p7,
       bcd_to_7_segment_decoder_1_p8, bcd_to_7_segment_decoder_1_p9, bcd_to_7_segment_decoder_1_p10,
       bcd_to_7_segment_decoder_1_p11, j_k_ff_1_q, j_k_ff_1_qn, j_k_ff_2_q, j_k_ff_2_qn, j_k_ff_3_q,
       j_k_ff_3_qn, j_k_ff_4_q, not_1_out;

  J_K_Flip_Flop #(.trigger("rising")) j_k_ff_1 (
    .J(Data), .clk(CLK), .K(not_1_out), .Q(j_k_ff_1_q), .Qn(j_k_ff_1_qn), .reset(CLR));  // open: preset, en
  not not_1 (not_1_out, Data);
  J_K_Flip_Flop #(.trigger("rising")) j_k_ff_2 (
    .J(j_k_ff_1_q), .clk(CLK), .K(j_k_ff_1_qn), .Q(j_k_ff_2_q), .Qn(j_k_ff_2_qn), .reset(CLR));  // open: preset, en
  J_K_Flip_Flop #(.trigger("rising")) j_k_ff_3 (
    .J(j_k_ff_2_q), .clk(CLK), .K(j_k_ff_2_qn), .Q(j_k_ff_3_q), .Qn(j_k_ff_3_qn), .reset(CLR));  // open: preset, en
  J_K_Flip_Flop #(.trigger("rising")) j_k_ff_4 (
    .J(j_k_ff_3_q), .clk(CLK), .K(j_k_ff_3_qn), .Q(j_k_ff_4_q), .reset(CLR));  // open: Qn, preset, en
  // BCD_to_7_segment_decoder bcd_to_7_segment_decoder_1: pin names not known; wires that end beside it: j_k_ff_4_q, j_k_ff_3_q, j_k_ff_2_q, j_k_ff_1_q, bcd_to_7_segment_decoder_1_p5, bcd_to_7_segment_decoder_1_p6, bcd_to_7_segment_decoder_1_p7, bcd_to_7_segment_decoder_1_p8, bcd_to_7_segment_decoder_1_p9, bcd_to_7_segment_decoder_1_p10, bcd_to_7_segment_decoder_1_p11
  _7_Segment_Display u_7_segment_display_1 (
    .g(bcd_to_7_segment_decoder_1_p11), .f(bcd_to_7_segment_decoder_1_p10),
    .a(bcd_to_7_segment_decoder_1_p5), .b(bcd_to_7_segment_decoder_1_p6), .e(bcd_to_7_segment_decoder_1_p9),
    .d(bcd_to_7_segment_decoder_1_p8), .c(bcd_to_7_segment_decoder_1_p7));  // open: dp

  // Notes on the sheet:
  //   Shift Register Using JK Flip-Flops
endmodule
